# Fritzing sketch Input sequence puzzle - wiring (saved by Fritzing 0.9.3b)
breadboards: 1

parts:
  LED2 = LED - 5mm [color="Red (633nm)" package="5 mm [THT]"]
  LED5 = LED - 5mm [color="Red (633nm)" package="5 mm [THT]"]
  S1 = Pushbutton [package="[THT]"]
  LED1 = LED - 5mm [color="Red (633nm)" package="5 mm [THT]"]
  R5 = Resistor [tolerance=±5% resistance=150 package=THT]
  WeMos_D1_R1 = WeMos D1 R2
  R2 = Resistor [tolerance=±5% resistance=150 package=THT]
  R4 = Resistor [tolerance=±5% resistance=150 package=THT]
  R1 = Resistor [tolerance=±5% resistance=150 package=THT]
  LED4 = LED - 5mm [color="Red (633nm)" package="5 mm [THT]"]
  KY-1 = Keyes Relay [package=THT]
  S3 = Pushbutton [package="[THT]"]
  S2 = Pushbutton [package="[THT]"]
  LED3 = LED - 5mm [color="Red (633nm)" package="5 mm [THT]"]
  R3 = Resistor [tolerance=±5% resistance=150 package=THT]

nets:
  N1: LED2.cathode, LED5.cathode, S1.Pin_1, S1.Pin_2, LED1.cathode, WeMos_D1_R1.GND#20, LED4.cathode, S3.Pin_1, S3.Pin_2, S2.Pin_1, S2.Pin_2, LED3.cathode
  N2: LED2.anode, R2.Pin_0
  N3: LED5.anode, R5.Pin_0
  N4: S1.Pin_3, S1.Pin_4, WeMos_D1_R1.D9
  N5: LED1.anode, R1.Pin_0
  N6: R5.Pin_1, WeMos_D1_R1.(D6)
  N7: WeMos_D1_R1.D2, R1.Pin_1
  N8: WeMos_D1_R1.D3, R2.Pin_1
  N9: WeMos_D1_R1.D4, R3.Pin_1
  N10: WeMos_D1_R1.(D5), R4.Pin_1
  N11: WeMos_D1_R1.(D7), S3.Pin_3, S3.Pin_4
  N12: WeMos_D1_R1.D8, S2.Pin_3, S2.Pin_4
  N13: WeMos_D1_R1.D10, KY-1.signal
  N14: WeMos_D1_R1.GND#15, KY-1.ground
  N15: WeMos_D1_R1.5V, KY-1.power
  N16: R4.Pin_0, LED4.anode
  N17: LED3.anode, R3.Pin_0

custom parts:
  WeMos D1 R2: The D1 R2 is a mini wifi board based on the ESP-8266EX.
  Keyes Relay: The Keyes 5V relay module is suitable for SCM development, home appliance control. It uses a 5V~12V TIL control signal which can control DC / AC signal.
